// Logisim project tructruc.circ as structural Verilog
module main (
  input  A,
  input  in_2,
  input  B,
  input  in_4
);

  xor xor_1 (in_2, A, B);
  and and_1 (in_4, A, B);
endmodule
